# Fritzing sketch 132 Final Project (saved by Fritzing 0.9.3b)
breadboards: 1

parts:
  Part1 = Arduino Uno (Rev3)
  J1 = Basic Servo
  J2 = Basic Servo
  Part2 = Adafruit Pi Cobbler Plus [part_number="Adafruit #2029"]
  LED1 = LED - 5mm [color="Red (633nm)" package="5 mm [THT]"]
  LED2 = LED - 5mm [color="Red (633nm)" package="5 mm [THT]"]
  LED3 = LED - 5mm [color="Red (633nm)" package="5 mm [THT]"]
  R1 = Resistor [tolerance=±5% resistance=220 package=THT]
  R2 = Resistor [tolerance=±5% resistance=220 package=THT]
  R3 = Resistor [tolerance=±5% resistance=220 package=THT]
  R4 = Resistor [tolerance=±5% resistance=220 package=THT]
  R5 = Resistor [tolerance=±5% resistance=220 package=THT]

nets:
  N1: Part1.A4/SDA, R4.Pin_1, R5.Pin_1
  N2: Part1.D2, J2.pulse
  N3: Part1.D4, J1.pulse
  VCC: Part1.5V, J1.vcc, J2.vcc, R4.Pin_0
  GND: Part1.GND, J1.gnd, J2.gnd, R5.Pin_0
  N4: Part2.GPIO4, Part2.TXD
  N5: Part2.GND, Part2.GPIO5, Part2.GPIO13, Part2.CE1, Part2.SCL, Part2.RXD, Part2.GPIO27, Part2.MOSI, Part2.GPIO21, R1.Pin_1, R2.Pin_1, R3.Pin_1
  N6: Part2.GPIO17, Part2.GPIO18, LED1.cathode
  +3.3V: Part2.+3.3V, Part2.GPIO24, Part2.+5V, Part2.SDA, LED3.cathode
  N7: Part2.MISO, Part2.GPIO25
  N8: Part2.SCLK, Part2.CE0
  N9: Part2.EEDAT, Part2.EECLK
  N10: Part2.GPIO6, Part2.GPIO12
  N11: Part2.GPIO19, Part2.GPIO16
  N12: Part2.GPIO26, Part2.GPIO20
  N13: Part2.GPIO23, Part2.GPIO22, LED2.cathode
  N14: LED1.anode, R1.Pin_0
  N15: LED2.anode, R2.Pin_0
  N16: LED3.anode, R3.Pin_0

custom parts:
  Adafruit Pi Cobbler Plus: The Raspberry Pi B+/Pi 2/ Pi 3 has landed on the Maker World like a 40-GPIO pinned, quad-USB ported, credit card sized bomb of DIY joy. And while you can use most of our great Model B accessories by hooking up our downgrade cable, its probably a good time to upgrade your set up and accessorize using all of the Model B+'s / Pi 2's / Pi 3's 40 pins. That's why we now carry the Adafruit Assembled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
